# Fritzing sketch SoilMoistoreSensor_v0.1 (saved by Fritzing 0.9.3b)
breadboards: 1

parts:
  Part1 = Soil Moisture Sensor
  WeMos_D1_Mini2 = WeMos D1 Mini
  Q1 = NPN-Transistor [package="TO92 [THT]"]
  R2 = Resistor [tolerance=±5% resistance=100 package="0603 [SMD]"]
  R1 = Resistor [tolerance=±5% resistance=1k package="2512 [SMD]"]

nets:
  N1: Part1.SIG, WeMos_D1_Mini2.A0
  N2: Part1.GND, WeMos_D1_Mini2.G, Q1.E
  N3: Part1.VCC, Q1.B, R2.Pin_1
  N4: WeMos_D1_Mini2.3V3, R2.Pin_0
  N5: WeMos_D1_Mini2.D2, R1.Pin_0
  N6: Q1.C, R1.Pin_1

notes:
  Soil Moisture Sensor using ESP8266
  Emitter connected to Ground
  Collector connected to Vcc of Sensor
  Collector connected to 3v3
  Grounding the Soil Moisture Sensor
  Base connected to Digital Pin (For Switching) through 1K Ohm Resistor
  NodeMCU or Wemos D1 Pro/Mini
