# Fritzing sketch SoilMoistureSensor_v0.11 (saved by Fritzing 0.9.3b)
breadboards: 1

parts:
  Part1 = Soil Moisture Sensor
  Q1 = NPN-Transistor [package="TO92 [THT]"]
  R2 = Resistor [tolerance=±5% resistance=100 package="0603 [SMD]"]
  R1 = Resistor [tolerance=±5% resistance=1k package="2512 [SMD]"]
  U1 = NodeMCU V1.0

nets:
  N1: Part1.SIG, U1.A0
  GND: Part1.GND, Q1.E, U1.GND
  N2: Part1.VCC, Q1.B, R2.Pin_1
  N3: Q1.C, R1.Pin_1
  N4: R2.Pin_0, U1.3V3
  N5: R1.Pin_0, U1.D2, U1.D3

notes:
  Soil Moisture Sensor using ESP8266
  Emitter connected to Ground
  Collector connected to Vcc of Sensor
  Collector connected to 3v3
  Grounding the Soil Moisture Sensor
  Base connected to Digital Pin (For Switching) through 1K Ohm Resistor
  NodeMCU or Wemos D1 Pro/Mini
  3v3
  AD0
  D2
  GND

custom parts:
  NodeMCU V1.0: ESP8266 based NodeMCU V1.0
